// Logisim project 2.circ as structural Verilog: 11 circuits, main circuit main
module main (
);

  wire _1c1, _1c2, _1c3, _1c4, _1c5, _1c6, _1c7, _1c8, _1colod, _2c1, _2c2, _2c3, _2c4, _2c5, _2c6, _2c7,
       _2c8, _2c9, _2colod, _3c1, _3c2, _3c3, _3c4, _3c5, _3c6, _3c7, _3c8, _3c9, _3c10, _3colod, _4c1, _4c2,
       _4c3, _4c4, _4c5, _4c6, _4c7, _4c8, _4c9, _4c10, _4c11, _4colod, _5c1, _5c2, _5c3, _5c4, _5c5, _5c6,
       _5c7, _5c8, _5c9, _5c10, _5c11, _5c12, _5colod, _6c1, _6c2, _6c3, _6c4, _6c5, _6c6, _6c7, _6c8, _6c9,
       _6c10, _6c11, _6c12, _6c13, _6colod, _7c1, _7c2, _7c3, _7c4, _7c5, _7c6, _7c7, _7c8, _7c9, _7c10,
       _7c11, _7c12, _7c13, _7c14, _7colod, and_2_out, Clock, comparator_1_eq, controlled_buffer_5_out,
       d_ff_1_q, data_ins, data_o, gen_done, generator_1_gen_done, generator_1_l_d, IAck, ins_p, IO_o,
       memory, not_1_out, pull_resistor_1_node, read_write, reset, undriven, vector_p,
       write_sentinels_1_clock_gen, write_sentinels_1_l_d;
  wire [0:0] and_1_out;
  wire [3:0] controlled_buffer_1_out, undriven_2;
  wire [7:0] addr, buffer_1_out, cdm_8_mark5_1_p1, cdm_8_mark5_1_p10, cdm_8_mark5_1_p11,
       controlled_buffer_8_out, data_base, generator_1_address, generator_1_data, ram_1_data, undriven_3,
       write_sentinels_1_address, write_sentinels_1_data;

  _1_colod u_1_colod_1 (
    ._1(_1c1), ._2(_1c2), ._3(_1c3), ._4(_1c4), ._5(_1c5), ._6(_1c6), ._7(_1c7), ._8(_1c8), .clock(Clock),
    .move_done(IAck));  // open: out_11
  D_Flip_Flop d_ff_1 (.Q(d_ff_1_q), .preset(undriven), .reset(IAck));  // open: clk, D, Qn, en
  and and_1 (and_1_out[0], addr[4], addr[5], addr[6], addr[7]);
  assign controlled_buffer_1_out = and_2_out ? undriven_2 : 4'bz;  // Controlled_Buffer controlled_buffer_1
  and and_2 (and_2_out, comparator_1_eq, IO_o);
  Button button_1 (.out(reset));
  _2_colod u_2_colod_1 (
    ._1(_2c1), ._2(_2c2), ._3(_2c3), ._4(_2c4), ._5(_2c5), ._6(_2c6), ._7(_2c7), ._8(_2c8), ._9(_2c9),
    .clock(Clock), .move_done(IAck));  // open: out_12
  Clock clock_1 (.out(Clock));
  Decoder #(.select(2), .disabled(0)) decoder_1 (
    .out0(ins_p), .out1(vector_p), .out2(data_o), .out3(IO_o), .sel({data_ins, and_1_out[0]}), .en(memory));
  Comparator comparator_1 (.a(cdm_8_mark5_1_p1), .b(undriven_3), .eq(comparator_1_eq));  // open: gt, lt
  _3_colod u_3_colod_1 (
    ._1(_3c1), ._2(_3c2), ._3(_3c3), ._4(_3c4), ._5(_3c5), ._6(_3c6), ._7(_3c7), ._8(_3c8), ._9(_3c9),
    ._10(_3c10), .clock(Clock), .move_done(IAck));  // open: out_13
  // CdM_8_mark5 cdm_8_mark5_1: pin names not known; wires that end beside it: cdm_8_mark5_1_p1, d_ff_1_q, 3'b000, IAck, Clock, data_ins, memory, read_write, addr, cdm_8_mark5_1_p10, cdm_8_mark5_1_p11
  assign cdm_8_mark5_1_p11 = read_write ? data_base : 8'bz;  // Controlled_Buffer controlled_buffer_2
  assign data_base = not_1_out ? cdm_8_mark5_1_p10 : 8'bz;  // Controlled_Buffer controlled_buffer_3
  not not_1 (not_1_out, read_write);
  _4_colod u_4_colod_1 (
    ._1(_4c1), ._2(_4c2), ._3(_4c3), ._4(_4c4), ._5(_4c5), ._6(_4c6), ._7(_4c7), ._8(_4c8), ._9(_4c9),
    ._10(_4c10), ._11(_4c11), .clock(Clock), .move_done(IAck));  // open: out_14
  assign buffer_1_out = generator_1_address;  // Buffer buffer_1, 8 bits wide
  assign buffer_1_out = gen_done ? write_sentinels_1_address : 8'bz;  // Controlled_Buffer controlled_buffer_4
  _5_colod u_5_colod_1 (
    ._1(_5c1), ._2(_5c2), ._3(_5c3), ._4(_5c4), ._5(_5c5), ._6(_5c6), ._7(_5c7), ._8(_5c8), ._9(_5c9),
    ._10(_5c10), ._11(_5c11), ._12(_5c12), .clock(Clock), .move_done(IAck));  // open: out_15
  not not_2 (gen_done, generator_1_gen_done);
  assign controlled_buffer_5_out = gen_done ? write_sentinels_1_clock_gen : 1'bz;  // Controlled_Buffer controlled_buffer_5
  _6_colod u_6_colod_1 (
    ._1(_6c1), ._2(_6c2), ._3(_6c3), ._4(_6c4), ._5(_6c5), ._6(_6c6), ._7(_6c7), ._8(_6c8), ._9(_6c9),
    ._10(_6c10), ._11(_6c11), ._12(_6c12), ._13(_6c13), .clock(Clock), .move_done(IAck));  // open: out_16
  generator generator_1 (
    .clock(Clock), .reset(reset), .data(generator_1_data), .address(generator_1_address),
    .clock_gen(controlled_buffer_5_out), .l_d(generator_1_l_d), .gen_done(generator_1_gen_done));
  write_sentinels write_sentinels_1 (
    .data(write_sentinels_1_data), .clock(pull_resistor_1_node), .reset(reset),
    .address(write_sentinels_1_address), .clock_gen(write_sentinels_1_clock_gen), .l_d(write_sentinels_1_l_d));
  Pull_Resistor pull_resistor_1 (.node(pull_resistor_1_node));
  assign pull_resistor_1_node = gen_done ? Clock : 1'bz;  // Controlled_Buffer controlled_buffer_6
  _7_colod u_7_colod_1 (
    ._1(_7c1), ._2(_7c2), ._3(_7c3), ._4(_7c4), ._5(_7c5), ._6(_7c6), ._7(_7c7), ._8(_7c8), ._9(_7c9),
    ._10(_7c10), ._11(_7c11), ._12(_7c12), ._13(_7c13), ._14(_7c14), .clock(Clock), .move_done(IAck));  // open: out_17
  RAM ram_1 (
    .addr(buffer_1_out), .data(ram_1_data), .clk(controlled_buffer_5_out), .ld(generator_1_l_d), .clr(reset));  // open: sel
  assign ram_1_data = controlled_buffer_8_out;  // Buffer buffer_2, 8 bits wide
  assign generator_1_l_d = gen_done ? write_sentinels_1_l_d : 1'bz;  // Controlled_Buffer controlled_buffer_7
  assign controlled_buffer_8_out = gen_done ? write_sentinels_1_data : 8'bz;  // Controlled_Buffer controlled_buffer_8
  configuration configuration_1 ();  // open: colods, clock, final_colod, card
  assign controlled_buffer_8_out = generator_1_data;  // Buffer buffer_3, 8 bits wide
  write_sentinels write_sentinels_2 ();  // open: data, clock, reset, address, clock_gen, l_d
  Button button_2 (.out(_1colod));
  Hex_Digit_Display hex_digit_display_1 ();  // open: value, dp
  Hex_Digit_Display hex_digit_display_2 ();  // open: value, dp
  Hex_Digit_Display hex_digit_display_3 ();  // open: value, dp
  Hex_Digit_Display hex_digit_display_4 ();  // open: value, dp
  Hex_Digit_Display hex_digit_display_5 ();  // open: value, dp
  Hex_Digit_Display hex_digit_display_6 ();  // open: value, dp
  Hex_Digit_Display hex_digit_display_7 ();  // open: value, dp
  Hex_Digit_Display hex_digit_display_8 ();  // open: value, dp
  Button button_3 (.out(_2colod));
  Hex_Digit_Display hex_digit_display_9 ();  // open: value, dp
  Hex_Digit_Display hex_digit_display_10 ();  // open: value, dp
  Hex_Digit_Display hex_digit_display_11 ();  // open: value, dp
  Hex_Digit_Display hex_digit_display_12 ();  // open: value, dp
  Hex_Digit_Display hex_digit_display_13 ();  // open: value, dp
  Hex_Digit_Display hex_digit_display_14 ();  // open: value, dp
  Hex_Digit_Display hex_digit_display_15 ();  // open: value, dp
  Hex_Digit_Display hex_digit_display_16 ();  // open: value, dp
  Hex_Digit_Display hex_digit_display_17 ();  // open: value, dp
  Button button_4 (.out(_3colod));
  Hex_Digit_Display hex_digit_display_18 ();  // open: value, dp
  Hex_Digit_Display hex_digit_display_19 ();  // open: value, dp
  Hex_Digit_Display hex_digit_display_20 ();  // open: value, dp
  Hex_Digit_Display hex_digit_display_21 ();  // open: value, dp
  Hex_Digit_Display hex_digit_display_22 ();  // open: value, dp
  Hex_Digit_Display hex_digit_display_23 ();  // open: value, dp
  Hex_Digit_Display hex_digit_display_24 ();  // open: value, dp
  Hex_Digit_Display hex_digit_display_25 ();  // open: value, dp
  Hex_Digit_Display hex_digit_display_26 ();  // open: value, dp
  Hex_Digit_Display hex_digit_display_27 ();  // open: value, dp
  Button button_5 (.out(_4colod));
  Hex_Digit_Display hex_digit_display_28 ();  // open: value, dp
  Hex_Digit_Display hex_digit_display_29 ();  // open: value, dp
  Hex_Digit_Display hex_digit_display_30 ();  // open: value, dp
  Hex_Digit_Display hex_digit_display_31 ();  // open: value, dp
  Hex_Digit_Display hex_digit_display_32 ();  // open: value, dp
  Hex_Digit_Display hex_digit_display_33 ();  // open: value, dp
  Hex_Digit_Display hex_digit_display_34 ();  // open: value, dp
  Hex_Digit_Display hex_digit_display_35 ();  // open: value, dp
  Hex_Digit_Display hex_digit_display_36 ();  // open: value, dp
  Hex_Digit_Display hex_digit_display_37 ();  // open: value, dp
  Hex_Digit_Display hex_digit_display_38 ();  // open: value, dp
  Button button_6 (.out(_5colod));
  Hex_Digit_Display hex_digit_display_39 ();  // open: value, dp
  Hex_Digit_Display hex_digit_display_40 ();  // open: value, dp
  Hex_Digit_Display hex_digit_display_41 ();  // open: value, dp
  Hex_Digit_Display hex_digit_display_42 ();  // open: value, dp
  Hex_Digit_Display hex_digit_display_43 ();  // open: value, dp
  Hex_Digit_Display hex_digit_display_44 ();  // open: value, dp
  Hex_Digit_Display hex_digit_display_45 ();  // open: value, dp
  Hex_Digit_Display hex_digit_display_46 ();  // open: value, dp
  Hex_Digit_Display hex_digit_display_47 ();  // open: value, dp
  Hex_Digit_Display hex_digit_display_48 ();  // open: value, dp
  Hex_Digit_Display hex_digit_display_49 ();  // open: value, dp
  Hex_Digit_Display hex_digit_display_50 ();  // open: value, dp
  Button button_7 (.out(_6colod));
  Hex_Digit_Display hex_digit_display_51 ();  // open: value, dp
  Hex_Digit_Display hex_digit_display_52 ();  // open: value, dp
  Hex_Digit_Display hex_digit_display_53 ();  // open: value, dp
  Hex_Digit_Display hex_digit_display_54 ();  // open: value, dp
  Hex_Digit_Display hex_digit_display_55 ();  // open: value, dp
  Hex_Digit_Display hex_digit_display_56 ();  // open: value, dp
  Hex_Digit_Display hex_digit_display_57 ();  // open: value, dp
  Hex_Digit_Display hex_digit_display_58 ();  // open: value, dp
  Hex_Digit_Display hex_digit_display_59 ();  // open: value, dp
  Hex_Digit_Display hex_digit_display_60 ();  // open: value, dp
  Hex_Digit_Display hex_digit_display_61 ();  // open: value, dp
  Hex_Digit_Display hex_digit_display_62 ();  // open: value, dp
  Hex_Digit_Display hex_digit_display_63 ();  // open: value, dp
  Button button_8 (.out(_7colod));
  Hex_Digit_Display hex_digit_display_64 ();  // open: value, dp
  Hex_Digit_Display hex_digit_display_65 ();  // open: value, dp
  Hex_Digit_Display hex_digit_display_66 ();  // open: value, dp
  Hex_Digit_Display hex_digit_display_67 ();  // open: value, dp
  Hex_Digit_Display hex_digit_display_68 ();  // open: value, dp
  Hex_Digit_Display hex_digit_display_69 ();  // open: value, dp
  Hex_Digit_Display hex_digit_display_70 ();  // open: value, dp
  Hex_Digit_Display hex_digit_display_71 ();  // open: value, dp
  Hex_Digit_Display hex_digit_display_72 ();  // open: value, dp
  Hex_Digit_Display hex_digit_display_73 ();  // open: value, dp
  Hex_Digit_Display hex_digit_display_74 ();  // open: value, dp
  Hex_Digit_Display hex_digit_display_75 ();  // open: value, dp
  Hex_Digit_Display hex_digit_display_76 ();  // open: value, dp
  Hex_Digit_Display hex_digit_display_77 ();  // open: value, dp
endmodule

module _1_colod (
  input  _1,
  input  _2,
  input  _3,
  input  _4,
  input  _5,
  input  _6,
  input  _7,
  input  _8,
  input  clock,
  input  move_done,
  output [7:0] out_11
);

  wire not_1_out, not_2_out, not_3_out, not_4_out, not_5_out, not_6_out, not_7_out, not_8_out, q1, q2, q3,
       q4, q5, q6, q7, q8;
  wire [2:0] priority_encoder_1_out;
  wire [7:0] bit_extender_1_out;

  D_Flip_Flop d_ff_1 (.clk(clock), .D(_1), .Q(q1), .en(not_1_out), .reset(move_done));  // open: Qn, preset
  not not_1 (not_1_out, q1);
  D_Flip_Flop d_ff_2 (.clk(clock), .D(_2), .Q(q2), .en(not_2_out), .reset(move_done));  // open: Qn, preset
  not not_2 (not_2_out, q2);
  D_Flip_Flop d_ff_3 (.clk(clock), .D(_3), .Q(q3), .en(not_3_out), .reset(move_done));  // open: Qn, preset
  not not_3 (not_3_out, q3);
  D_Flip_Flop d_ff_4 (.clk(clock), .D(_4), .Q(q4), .en(not_4_out), .reset(move_done));  // open: Qn, preset
  not not_4 (not_4_out, q4);
  D_Flip_Flop d_ff_5 (.clk(clock), .D(_5), .Q(q5), .en(not_5_out), .reset(move_done));  // open: Qn, preset
  not not_5 (not_5_out, q5);
  D_Flip_Flop d_ff_6 (.clk(clock), .D(_6), .Q(q6), .en(not_6_out), .reset(move_done));  // open: Qn, preset
  not not_6 (not_6_out, q6);
  D_Flip_Flop d_ff_7 (.clk(clock), .D(_7), .Q(q7), .en(not_7_out), .reset(move_done));  // open: Qn, preset
  not not_7 (not_7_out, q7);
  D_Flip_Flop d_ff_8 (.clk(clock), .D(_8), .Q(q8), .en(not_8_out), .reset(move_done));  // open: Qn, preset
  not not_8 (not_8_out, q8);
  Priority_Encoder priority_encoder_1 (
    .in0(q1), .in1(q2), .in2(q3), .in3(q4), .in4(q5), .in5(q6), .in6(q7), .in7(q8),
    .out(priority_encoder_1_out));  // open: en_in, gs, en_out
  assign bit_extender_1_out = {{5{1'b0}}, priority_encoder_1_out};  // Bit_Extender bit_extender_1
  Adder adder_1 (.a(8'h80), .b(bit_extender_1_out), .out(out_11));  // open: cin, cout

  // Other names for the same wires on the sheet: d = move_done
endmodule

module _2_colod (
  input  _1,
  input  _2,
  input  _3,
  input  _4,
  input  _5,
  input  _6,
  input  _7,
  input  _8,
  input  _9,
  input  clock,
  input  move_done,
  output [7:0] out_12
);

  wire not_1_out, not_2_out, not_3_out, not_4_out, not_5_out, not_6_out, not_7_out, not_8_out, not_9_out, q1,
       q2, q3, q4, q5, q6, q7, q8, q9;
  wire [3:0] priority_encoder_1_out;
  wire [7:0] bit_extender_1_out;

  D_Flip_Flop d_ff_1 (.clk(clock), .D(_1), .Q(q1), .en(not_1_out), .reset(move_done));  // open: Qn, preset
  not not_1 (not_1_out, q1);
  D_Flip_Flop d_ff_2 (.clk(clock), .D(_2), .Q(q2), .en(not_2_out), .reset(move_done));  // open: Qn, preset
  not not_2 (not_2_out, q2);
  D_Flip_Flop d_ff_3 (.clk(clock), .D(_3), .Q(q3), .en(not_3_out), .reset(move_done));  // open: Qn, preset
  not not_3 (not_3_out, q3);
  D_Flip_Flop d_ff_4 (.clk(clock), .D(_4), .Q(q4), .en(not_4_out), .reset(move_done));  // open: Qn, preset
  not not_4 (not_4_out, q4);
  D_Flip_Flop d_ff_5 (.clk(clock), .D(_5), .Q(q5), .en(not_5_out), .reset(move_done));  // open: Qn, preset
  not not_5 (not_5_out, q5);
  D_Flip_Flop d_ff_6 (.clk(clock), .D(_6), .Q(q6), .en(not_6_out), .reset(move_done));  // open: Qn, preset
  not not_6 (not_6_out, q6);
  D_Flip_Flop d_ff_7 (.clk(clock), .D(_7), .Q(q7), .en(not_7_out), .reset(move_done));  // open: Qn, preset
  not not_7 (not_7_out, q7);
  D_Flip_Flop d_ff_8 (.clk(clock), .D(_8), .Q(q8), .en(not_8_out), .reset(move_done));  // open: Qn, preset
  not not_8 (not_8_out, q8);
  D_Flip_Flop d_ff_9 (.clk(clock), .D(_9), .Q(q9), .en(not_9_out), .reset(move_done));  // open: Qn, preset
  not not_9 (not_9_out, q9);
  Priority_Encoder #(.select(4)) priority_encoder_1 (
    .in0(q1), .in1(q2), .in2(q3), .in3(q4), .in4(q5), .in5(q6), .in6(q7), .in7(q8), .in8(q9), .in9(1'b0),
    .in10(1'b0), .in11(1'b0), .in12(1'b0), .in13(1'b0), .in14(1'b0), .in15(1'b0), .out(priority_encoder_1_out));  // open: gs, en_out, en_in
  assign bit_extender_1_out = {{4{1'b0}}, priority_encoder_1_out};  // Bit_Extender bit_extender_1
  Adder adder_1 (.a(8'h80), .b(bit_extender_1_out), .out(out_12));  // open: cin, cout

  // Other names for the same wires on the sheet: d = move_done
endmodule

module _3_colod (
  input  _1,
  input  _2,
  input  _3,
  input  _4,
  input  _5,
  input  _6,
  input  _7,
  input  _8,
  input  _9,
  input  _10,
  input  clock,
  input  move_done,
  output [7:0] out_13
);

  wire not_1_out, not_2_out, not_3_out, not_4_out, not_5_out, not_6_out, not_7_out, not_8_out, not_9_out,
       not_10_out, q1, q2, q3, q4, q5, q6, q7, q8, q9, q10;
  wire [3:0] priority_encoder_1_out;
  wire [7:0] bit_extender_1_out;

  D_Flip_Flop d_ff_1 (.clk(clock), .D(_1), .Q(q1), .en(not_1_out), .reset(move_done));  // open: Qn, preset
  not not_1 (not_1_out, q1);
  D_Flip_Flop d_ff_2 (.clk(clock), .D(_2), .Q(q2), .en(not_2_out), .reset(move_done));  // open: Qn, preset
  not not_2 (not_2_out, q2);
  D_Flip_Flop d_ff_3 (.clk(clock), .D(_3), .Q(q3), .en(not_3_out), .reset(move_done));  // open: Qn, preset
  not not_3 (not_3_out, q3);
  D_Flip_Flop d_ff_4 (.clk(clock), .D(_4), .Q(q4), .en(not_4_out), .reset(move_done));  // open: Qn, preset
  not not_4 (not_4_out, q4);
  D_Flip_Flop d_ff_5 (.clk(clock), .D(_5), .Q(q5), .en(not_5_out), .reset(move_done));  // open: Qn, preset
  not not_5 (not_5_out, q5);
  D_Flip_Flop d_ff_6 (.clk(clock), .D(_6), .Q(q6), .en(not_6_out), .reset(move_done));  // open: Qn, preset
  not not_6 (not_6_out, q6);
  D_Flip_Flop d_ff_7 (.clk(clock), .D(_7), .Q(q7), .en(not_7_out), .reset(move_done));  // open: Qn, preset
  not not_7 (not_7_out, q7);
  D_Flip_Flop d_ff_8 (.clk(clock), .D(_8), .Q(q8), .en(not_8_out), .reset(move_done));  // open: Qn, preset
  not not_8 (not_8_out, q8);
  D_Flip_Flop d_ff_9 (.clk(clock), .D(_9), .Q(q9), .en(not_9_out), .reset(move_done));  // open: Qn, preset
  not not_9 (not_9_out, q9);
  D_Flip_Flop d_ff_10 (.clk(clock), .D(_10), .Q(q10), .en(not_10_out), .reset(move_done));  // open: Qn, preset
  not not_10 (not_10_out, q10);
  Priority_Encoder #(.select(4)) priority_encoder_1 (
    .in0(q1), .in1(q2), .in2(q3), .in3(q4), .in4(q5), .in5(q6), .in6(q7), .in7(q8), .in8(q9), .in9(q10),
    .in10(1'b0), .in11(1'b0), .in12(1'b0), .in13(1'b0), .in14(1'b0), .in15(1'b0), .out(priority_encoder_1_out));  // open: gs, en_out, en_in
  assign bit_extender_1_out = {{4{1'b0}}, priority_encoder_1_out};  // Bit_Extender bit_extender_1
  Adder adder_1 (.a(8'h80), .b(bit_extender_1_out), .out(out_13));  // open: cin, cout

  // Other names for the same wires on the sheet: d = move_done
endmodule

module _4_colod (
  input  _1,
  input  _2,
  input  _3,
  input  _4,
  input  _5,
  input  _6,
  input  _7,
  input  _8,
  input  _9,
  input  _10,
  input  _11,
  input  clock,
  input  move_done,
  output [7:0] out_14
);

  wire not_1_out, not_2_out, not_3_out, not_4_out, not_5_out, not_6_out, not_7_out, not_8_out, not_9_out,
       not_10_out, not_11_out, q1, q2, q3, q4, q5, q6, q7, q8, q9, q10, q11;
  wire [3:0] priority_encoder_1_out;
  wire [7:0] bit_extender_1_out;

  D_Flip_Flop d_ff_1 (.clk(clock), .D(_1), .Q(q1), .en(not_1_out), .reset(move_done));  // open: Qn, preset
  not not_1 (not_1_out, q1);
  D_Flip_Flop d_ff_2 (.clk(clock), .D(_2), .Q(q2), .en(not_2_out), .reset(move_done));  // open: Qn, preset
  not not_2 (not_2_out, q2);
  D_Flip_Flop d_ff_3 (.clk(clock), .D(_3), .Q(q3), .en(not_3_out), .reset(move_done));  // open: Qn, preset
  not not_3 (not_3_out, q3);
  D_Flip_Flop d_ff_4 (.clk(clock), .D(_4), .Q(q4), .en(not_4_out), .reset(move_done));  // open: Qn, preset
  not not_4 (not_4_out, q4);
  D_Flip_Flop d_ff_5 (.clk(clock), .D(_5), .Q(q5), .en(not_5_out), .reset(move_done));  // open: Qn, preset
  not not_5 (not_5_out, q5);
  D_Flip_Flop d_ff_6 (.clk(clock), .D(_6), .Q(q6), .en(not_6_out), .reset(move_done));  // open: Qn, preset
  not not_6 (not_6_out, q6);
  D_Flip_Flop d_ff_7 (.clk(clock), .D(_7), .Q(q7), .en(not_7_out), .reset(move_done));  // open: Qn, preset
  not not_7 (not_7_out, q7);
  D_Flip_Flop d_ff_8 (.clk(clock), .D(_8), .Q(q8), .en(not_8_out), .reset(move_done));  // open: Qn, preset
  not not_8 (not_8_out, q8);
  D_Flip_Flop d_ff_9 (.clk(clock), .D(_9), .Q(q9), .en(not_9_out), .reset(move_done));  // open: Qn, preset
  not not_9 (not_9_out, q9);
  D_Flip_Flop d_ff_10 (.clk(clock), .D(_10), .Q(q10), .en(not_10_out), .reset(move_done));  // open: Qn, preset
  not not_10 (not_10_out, q10);
  D_Flip_Flop d_ff_11 (.clk(clock), .D(_11), .Q(q11), .en(not_11_out), .reset(move_done));  // open: Qn, preset
  not not_11 (not_11_out, q11);
  Priority_Encoder #(.select(4)) priority_encoder_1 (
    .in0(q1), .in1(q2), .in2(q3), .in3(q4), .in4(q5), .in5(q6), .in6(q7), .in7(q8), .in8(q9), .in9(q10),
    .in10(q11), .in11(1'b0), .in12(1'b0), .in13(1'b0), .in14(1'b0), .in15(1'b0), .out(priority_encoder_1_out));  // open: gs, en_out, en_in
  assign bit_extender_1_out = {{4{1'b0}}, priority_encoder_1_out};  // Bit_Extender bit_extender_1
  Adder adder_1 (.a(8'h80), .b(bit_extender_1_out), .out(out_14));  // open: cin, cout

  // Other names for the same wires on the sheet: d = move_done
endmodule

module _5_colod (
  input  _1,
  input  _2,
  input  _3,
  input  _4,
  input  _5,
  input  _6,
  input  _7,
  input  _8,
  input  _9,
  input  _10,
  input  _11,
  input  _12,
  input  clock,
  input  move_done,
  output [7:0] out_15
);

  wire not_1_out, not_2_out, not_3_out, not_4_out, not_5_out, not_6_out, not_7_out, not_8_out, not_9_out,
       not_10_out, not_11_out, not_12_out, q1, q2, q3, q4, q5, q6, q7, q8, q9, q10, q11, q12;
  wire [3:0] priority_encoder_1_out;
  wire [7:0] bit_extender_1_out;

  D_Flip_Flop d_ff_1 (.clk(clock), .D(_1), .Q(q1), .en(not_1_out), .reset(move_done));  // open: Qn, preset
  not not_1 (not_1_out, q1);
  D_Flip_Flop d_ff_2 (.clk(clock), .D(_2), .Q(q2), .en(not_2_out), .reset(move_done));  // open: Qn, preset
  not not_2 (not_2_out, q2);
  D_Flip_Flop d_ff_3 (.clk(clock), .D(_3), .Q(q3), .en(not_3_out), .reset(move_done));  // open: Qn, preset
  not not_3 (not_3_out, q3);
  D_Flip_Flop d_ff_4 (.clk(clock), .D(_4), .Q(q4), .en(not_4_out), .reset(move_done));  // open: Qn, preset
  not not_4 (not_4_out, q4);
  D_Flip_Flop d_ff_5 (.clk(clock), .D(_5), .Q(q5), .en(not_5_out), .reset(move_done));  // open: Qn, preset
  not not_5 (not_5_out, q5);
  D_Flip_Flop d_ff_6 (.clk(clock), .D(_6), .Q(q6), .en(not_6_out), .reset(move_done));  // open: Qn, preset
  not not_6 (not_6_out, q6);
  D_Flip_Flop d_ff_7 (.clk(clock), .D(_7), .Q(q7), .en(not_7_out), .reset(move_done));  // open: Qn, preset
  not not_7 (not_7_out, q7);
  D_Flip_Flop d_ff_8 (.clk(clock), .D(_8), .Q(q8), .en(not_8_out), .reset(move_done));  // open: Qn, preset
  not not_8 (not_8_out, q8);
  D_Flip_Flop d_ff_9 (.clk(clock), .D(_9), .Q(q9), .en(not_9_out), .reset(move_done));  // open: Qn, preset
  not not_9 (not_9_out, q9);
  D_Flip_Flop d_ff_10 (.clk(clock), .D(_10), .Q(q10), .en(not_10_out), .reset(move_done));  // open: Qn, preset
  not not_10 (not_10_out, q10);
  D_Flip_Flop d_ff_11 (.clk(clock), .D(_11), .Q(q11), .en(not_11_out), .reset(move_done));  // open: Qn, preset
  not not_11 (not_11_out, q11);
  D_Flip_Flop d_ff_12 (.clk(clock), .D(_12), .Q(q12), .en(not_12_out), .reset(move_done));  // open: Qn, preset
  not not_12 (not_12_out, q12);
  Priority_Encoder #(.select(4)) priority_encoder_1 (
    .in0(q1), .in1(q2), .in2(q3), .in3(q4), .in4(q5), .in5(q6), .in6(q7), .in7(q8), .in8(q9), .in9(q10),
    .in10(q11), .in11(q12), .in12(1'b0), .in13(1'b0), .in14(1'b0), .in15(1'b0), .out(priority_encoder_1_out));  // open: gs, en_out, en_in
  assign bit_extender_1_out = {{4{1'b0}}, priority_encoder_1_out};  // Bit_Extender bit_extender_1
  Adder adder_1 (.a(8'h80), .b(bit_extender_1_out), .out(out_15));  // open: cin, cout

  // Other names for the same wires on the sheet: d = move_done
endmodule

module _6_colod (
  input  _1,
  input  _2,
  input  _3,
  input  _4,
  input  _5,
  input  _6,
  input  _7,
  input  _8,
  input  _9,
  input  _10,
  input  _11,
  input  _12,
  input  _13,
  input  clock,
  input  move_done,
  output [7:0] out_16
);

  wire not_1_out, not_2_out, not_3_out, not_4_out, not_5_out, not_6_out, not_7_out, not_8_out, not_9_out,
       not_10_out, not_11_out, not_12_out, not_13_out, q1, q2, q3, q4, q5, q6, q7, q8, q9, q10, q11, q12, q13;
  wire [3:0] priority_encoder_1_out;
  wire [7:0] bit_extender_1_out;

  D_Flip_Flop d_ff_1 (.clk(clock), .D(_1), .Q(q1), .en(not_1_out), .reset(move_done));  // open: Qn, preset
  not not_1 (not_1_out, q1);
  D_Flip_Flop d_ff_2 (.clk(clock), .D(_2), .Q(q2), .en(not_2_out), .reset(move_done));  // open: Qn, preset
  not not_2 (not_2_out, q2);
  D_Flip_Flop d_ff_3 (.clk(clock), .D(_3), .Q(q3), .en(not_3_out), .reset(move_done));  // open: Qn, preset
  not not_3 (not_3_out, q3);
  D_Flip_Flop d_ff_4 (.clk(clock), .D(_4), .Q(q4), .en(not_4_out), .reset(move_done));  // open: Qn, preset
  not not_4 (not_4_out, q4);
  D_Flip_Flop d_ff_5 (.clk(clock), .D(_5), .Q(q5), .en(not_5_out), .reset(move_done));  // open: Qn, preset
  not not_5 (not_5_out, q5);
  D_Flip_Flop d_ff_6 (.clk(clock), .D(_6), .Q(q6), .en(not_6_out), .reset(move_done));  // open: Qn, preset
  not not_6 (not_6_out, q6);
  D_Flip_Flop d_ff_7 (.clk(clock), .D(_7), .Q(q7), .en(not_7_out), .reset(move_done));  // open: Qn, preset
  not not_7 (not_7_out, q7);
  D_Flip_Flop d_ff_8 (.clk(clock), .D(_8), .Q(q8), .en(not_8_out), .reset(move_done));  // open: Qn, preset
  not not_8 (not_8_out, q8);
  D_Flip_Flop d_ff_9 (.clk(clock), .D(_9), .Q(q9), .en(not_9_out), .reset(move_done));  // open: Qn, preset
  not not_9 (not_9_out, q9);
  D_Flip_Flop d_ff_10 (.clk(clock), .D(_10), .Q(q10), .en(not_10_out), .reset(move_done));  // open: Qn, preset
  not not_10 (not_10_out, q10);
  D_Flip_Flop d_ff_11 (.clk(clock), .D(_11), .Q(q11), .en(not_11_out), .reset(move_done));  // open: Qn, preset
  not not_11 (not_11_out, q11);
  D_Flip_Flop d_ff_12 (.clk(clock), .D(_12), .Q(q12), .en(not_12_out), .reset(move_done));  // open: Qn, preset
  not not_12 (not_12_out, q12);
  D_Flip_Flop d_ff_13 (.clk(clock), .D(_13), .Q(q13), .en(not_13_out), .reset(move_done));  // open: Qn, preset
  not not_13 (not_13_out, q13);
  assign bit_extender_1_out = {{4{1'b0}}, priority_encoder_1_out};  // Bit_Extender bit_extender_1
  Priority_Encoder #(.select(4)) priority_encoder_1 (
    .in0(q1), .in1(q2), .in2(q3), .in3(q4), .in4(q5), .in5(q6), .in6(q7), .in7(q8), .in8(q9), .in9(q10),
    .in10(q11), .in11(q12), .in12(q13), .in13(1'b0), .in14(1'b0), .in15(1'b0), .out(priority_encoder_1_out));  // open: gs, en_out, en_in
  Adder adder_1 (.a(8'h80), .b(bit_extender_1_out), .out(out_16));  // open: cin, cout

  // Other names for the same wires on the sheet: d = move_done
endmodule

module _7_colod (
  input  _1,
  input  _2,
  input  _3,
  input  _4,
  input  _5,
  input  _6,
  input  _7,
  input  _8,
  input  _9,
  input  _10,
  input  _11,
  input  _12,
  input  _13,
  input  _14,
  input  clock,
  input  move_done,
  output [7:0] out_17
);

  wire not_1_out, not_2_out, not_3_out, not_4_out, not_5_out, not_6_out, not_7_out, not_8_out, not_9_out,
       not_10_out, not_11_out, not_12_out, not_13_out, not_14_out, q1, q2, q3, q4, q5, q6, q7, q8, q9, q10,
       q11, q12, q13, q14;
  wire [3:0] priority_encoder_1_out;
  wire [7:0] bit_extender_1_out;

  D_Flip_Flop d_ff_1 (.clk(clock), .D(_1), .Q(q1), .en(not_1_out), .reset(move_done));  // open: Qn, preset
  not not_1 (not_1_out, q1);
  D_Flip_Flop d_ff_2 (.clk(clock), .D(_2), .Q(q2), .en(not_2_out), .reset(move_done));  // open: Qn, preset
  not not_2 (not_2_out, q2);
  D_Flip_Flop d_ff_3 (.clk(clock), .D(_3), .Q(q3), .en(not_3_out), .reset(move_done));  // open: Qn, preset
  not not_3 (not_3_out, q3);
  D_Flip_Flop d_ff_4 (.clk(clock), .D(_4), .Q(q4), .en(not_4_out), .reset(move_done));  // open: Qn, preset
  not not_4 (not_4_out, q4);
  D_Flip_Flop d_ff_5 (.clk(clock), .D(_5), .Q(q5), .en(not_5_out), .reset(move_done));  // open: Qn, preset
  not not_5 (not_5_out, q5);
  D_Flip_Flop d_ff_6 (.clk(clock), .D(_6), .Q(q6), .en(not_6_out), .reset(move_done));  // open: Qn, preset
  not not_6 (not_6_out, q6);
  D_Flip_Flop d_ff_7 (.clk(clock), .D(_7), .Q(q7), .en(not_7_out), .reset(move_done));  // open: Qn, preset
  not not_7 (not_7_out, q7);
  D_Flip_Flop d_ff_8 (.clk(clock), .D(_8), .Q(q8), .en(not_8_out), .reset(move_done));  // open: Qn, preset
  not not_8 (not_8_out, q8);
  D_Flip_Flop d_ff_9 (.clk(clock), .D(_9), .Q(q9), .en(not_9_out), .reset(move_done));  // open: Qn, preset
  not not_9 (not_9_out, q9);
  D_Flip_Flop d_ff_10 (.clk(clock), .D(_10), .Q(q10), .en(not_10_out), .reset(move_done));  // open: Qn, preset
  not not_10 (not_10_out, q10);
  D_Flip_Flop d_ff_11 (.clk(clock), .D(_11), .Q(q11), .en(not_11_out), .reset(move_done));  // open: Qn, preset
  not not_11 (not_11_out, q11);
  D_Flip_Flop d_ff_12 (.clk(clock), .D(_12), .Q(q12), .en(not_12_out), .reset(move_done));  // open: Qn, preset
  not not_12 (not_12_out, q12);
  D_Flip_Flop d_ff_13 (.clk(clock), .D(_13), .Q(q13), .en(not_13_out), .reset(move_done));  // open: Qn, preset
  not not_13 (not_13_out, q13);
  D_Flip_Flop d_ff_14 (.clk(clock), .D(_14), .Q(q14), .en(not_14_out), .reset(move_done));  // open: Qn, preset
  not not_14 (not_14_out, q14);
  assign bit_extender_1_out = {{4{1'b0}}, priority_encoder_1_out};  // Bit_Extender bit_extender_1
  Priority_Encoder #(.select(4)) priority_encoder_1 (
    .in0(q1), .in1(q2), .in2(q3), .in3(q4), .in4(q5), .in5(q6), .in6(q7), .in7(q8), .in8(q9), .in9(q10),
    .in10(q11), .in11(q12), .in12(q13), .in13(q14), .in14(1'b0), .in15(1'b0), .out(priority_encoder_1_out));  // open: gs, en_out, en_in
  Adder adder_1 (.a(8'h80), .b(bit_extender_1_out), .out(out_17));  // open: cin, cout

  // Other names for the same wires on the sheet: d = move_done
endmodule

module configuration (
  input  [31:0] colods,
  input  clock,
  output [31:0] final_colod,
  output [3:0] card
);

  wire _1, _2, _3, _4, _5, _6, _7, _8, _9, _10, _11, _12, _13, _14, _15, _16, _17, _18, _19, _20, _21, _22,
       _23, _24, _25, _26, _27, _28, _29, _30, _31, _32, bitfinder_1_found, bitfinder_2_found,
       bitfinder_3_found, bitfinder_4_found, bitfinder_5_found, bitfinder_6_found, bitfinder_7_found,
       bitfinder_8_found, bitfinder_9_found, bitfinder_10_found, bitfinder_11_found, bitfinder_12_found,
       bitfinder_13_found, bitfinder_14_found, bitfinder_15_found, bitfinder_16_found, bitfinder_17_found,
       bitfinder_18_found, bitfinder_19_found, bitfinder_20_found, bitfinder_21_found, bitfinder_22_found,
       bitfinder_23_found, bitfinder_24_found, bitfinder_25_found, bitfinder_26_found, bitfinder_27_found,
       bitfinder_28_found, bitfinder_29_found, bitfinder_30_found, bitfinder_31_found, bitfinder_32_found;
  wire [3:0] pull_resistor_33_node, pull_resistor_34_node, pull_resistor_35_node, pull_resistor_36_node,
       pull_resistor_37_node, pull_resistor_38_node, pull_resistor_39_node, pull_resistor_40_node,
       pull_resistor_41_node, pull_resistor_42_node, pull_resistor_43_node, pull_resistor_44_node,
       pull_resistor_45_node, pull_resistor_46_node, pull_resistor_47_node, pull_resistor_48_node,
       pull_resistor_49_node, pull_resistor_50_node, pull_resistor_51_node, pull_resistor_52_node,
       pull_resistor_53_node, pull_resistor_54_node, pull_resistor_55_node, pull_resistor_56_node,
       pull_resistor_57_node, pull_resistor_58_node, pull_resistor_59_node, pull_resistor_60_node,
       pull_resistor_61_node, pull_resistor_62_node, pull_resistor_63_node, pull_resistor_64_node;
  wire [4:0] random_1_out;
  wire [31:0] n1, n2, n3, n4, n5, n6, n7, n8, n9, n10, n11, n12, n13, n14, n15, n16, n17, n18, n19, n20, n21,
       n22, n23, n24, n25, n26, n27, n28, n29, n30, n31, n32, nor_1_out, pull_resistor_1_node,
       pull_resistor_2_node, pull_resistor_3_node, pull_resistor_4_node, pull_resistor_5_node,
       pull_resistor_6_node, pull_resistor_7_node, pull_resistor_8_node, pull_resistor_9_node,
       pull_resistor_10_node, pull_resistor_11_node, pull_resistor_12_node, pull_resistor_13_node,
       pull_resistor_14_node, pull_resistor_15_node, pull_resistor_16_node, pull_resistor_17_node,
       pull_resistor_18_node, pull_resistor_19_node, pull_resistor_20_node, pull_resistor_21_node,
       pull_resistor_22_node, pull_resistor_23_node, pull_resistor_24_node, pull_resistor_25_node,
       pull_resistor_26_node, pull_resistor_27_node, pull_resistor_28_node, pull_resistor_29_node,
       pull_resistor_30_node, pull_resistor_31_node, pull_resistor_32_node;

  Decoder #(.select(5), .enable("false")) decoder_1 (
    .out0(_1), .out1(_2), .out2(_3), .out3(_4), .out4(_5), .out5(_6), .out6(_7), .out7(_8), .out8(_9),
    .out9(_10), .out10(_11), .out11(_12), .out12(_13), .out13(_14), .out14(_15), .out15(_16), .out16(_17),
    .out17(_18), .out18(_19), .out19(_20), .out20(_21), .out21(_22), .out22(_23), .out23(_24), .out24(_25),
    .out25(_26), .out26(_27), .out27(_28), .out28(_29), .out29(_30), .out30(_31), .out31(_32),
    .sel(random_1_out));
  Random #(.width(5)) random_1 (.clk(clock), .out(random_1_out));  // open: next, clr
  assign nor_1_out = ~(n1 | n2 | n3 | n4 | n5 | n6 | n7 | n8 | n9 | n10 | n11 | n12 | n13 | n14 | n15 | n16 | n17 | n18 | n19 | n20 | n21 | n22 | n23 | n24 | n25 | n26 | n27 | n28 | n29 | n30 | n31 | n32);  // NOR_Gate nor_1, 32 bits wide
  assign final_colod = nor_1_out & colods;  // AND_Gate and_1, 32 bits wide
  Pull_Resistor pull_resistor_1 (.node(pull_resistor_1_node));
  Pull_Resistor pull_resistor_2 (.node(pull_resistor_2_node));
  Pull_Resistor pull_resistor_3 (.node(pull_resistor_3_node));
  Pull_Resistor pull_resistor_4 (.node(pull_resistor_4_node));
  Pull_Resistor pull_resistor_5 (.node(pull_resistor_5_node));
  Pull_Resistor pull_resistor_6 (.node(pull_resistor_6_node));
  Pull_Resistor pull_resistor_7 (.node(pull_resistor_7_node));
  Pull_Resistor pull_resistor_8 (.node(pull_resistor_8_node));
  Pull_Resistor pull_resistor_9 (.node(pull_resistor_9_node));
  Pull_Resistor pull_resistor_10 (.node(pull_resistor_10_node));
  Pull_Resistor pull_resistor_11 (.node(pull_resistor_11_node));
  Pull_Resistor pull_resistor_12 (.node(pull_resistor_12_node));
  Pull_Resistor pull_resistor_13 (.node(pull_resistor_13_node));
  Pull_Resistor pull_resistor_14 (.node(pull_resistor_14_node));
  Pull_Resistor pull_resistor_15 (.node(pull_resistor_15_node));
  Pull_Resistor pull_resistor_16 (.node(pull_resistor_16_node));
  Pull_Resistor pull_resistor_17 (.node(pull_resistor_17_node));
  Pull_Resistor pull_resistor_18 (.node(pull_resistor_18_node));
  Pull_Resistor pull_resistor_19 (.node(pull_resistor_19_node));
  Pull_Resistor pull_resistor_20 (.node(pull_resistor_20_node));
  Pull_Resistor pull_resistor_21 (.node(pull_resistor_21_node));
  Pull_Resistor pull_resistor_22 (.node(pull_resistor_22_node));
  Pull_Resistor pull_resistor_23 (.node(pull_resistor_23_node));
  Pull_Resistor pull_resistor_24 (.node(pull_resistor_24_node));
  Pull_Resistor pull_resistor_25 (.node(pull_resistor_25_node));
  Pull_Resistor pull_resistor_26 (.node(pull_resistor_26_node));
  Pull_Resistor pull_resistor_27 (.node(pull_resistor_27_node));
  Pull_Resistor pull_resistor_28 (.node(pull_resistor_28_node));
  Pull_Resistor pull_resistor_29 (.node(pull_resistor_29_node));
  Pull_Resistor pull_resistor_30 (.node(pull_resistor_30_node));
  Pull_Resistor pull_resistor_31 (.node(pull_resistor_31_node));
  Pull_Resistor pull_resistor_32 (.node(pull_resistor_32_node));
  assign pull_resistor_1_node = _1 ? 32'h1 : 32'bz;  // Controlled_Buffer controlled_buffer_1
  assign pull_resistor_2_node = _2 ? 32'h2 : 32'bz;  // Controlled_Buffer controlled_buffer_2
  assign pull_resistor_3_node = _3 ? 32'h4 : 32'bz;  // Controlled_Buffer controlled_buffer_3
  assign pull_resistor_4_node = _4 ? 32'h8 : 32'bz;  // Controlled_Buffer controlled_buffer_4
  assign pull_resistor_5_node = _5 ? 32'h10 : 32'bz;  // Controlled_Buffer controlled_buffer_5
  assign pull_resistor_6_node = _6 ? 32'h20 : 32'bz;  // Controlled_Buffer controlled_buffer_6
  assign pull_resistor_7_node = _7 ? 32'h40 : 32'bz;  // Controlled_Buffer controlled_buffer_7
  assign pull_resistor_8_node = _8 ? 32'h80 : 32'bz;  // Controlled_Buffer controlled_buffer_8
  assign pull_resistor_9_node = _9 ? 32'h100 : 32'bz;  // Controlled_Buffer controlled_buffer_9
  assign pull_resistor_10_node = _10 ? 32'h200 : 32'bz;  // Controlled_Buffer controlled_buffer_10
  assign pull_resistor_11_node = _11 ? 32'h400 : 32'bz;  // Controlled_Buffer controlled_buffer_11
  assign pull_resistor_12_node = _12 ? 32'h800 : 32'bz;  // Controlled_Buffer controlled_buffer_12
  assign pull_resistor_13_node = _13 ? 32'h1000 : 32'bz;  // Controlled_Buffer controlled_buffer_13
  assign pull_resistor_14_node = _14 ? 32'h2000 : 32'bz;  // Controlled_Buffer controlled_buffer_14
  assign pull_resistor_15_node = _15 ? 32'h4000 : 32'bz;  // Controlled_Buffer controlled_buffer_15
  assign pull_resistor_16_node = _16 ? 32'h8000 : 32'bz;  // Controlled_Buffer controlled_buffer_16
  assign pull_resistor_17_node = _17 ? 32'h10000 : 32'bz;  // Controlled_Buffer controlled_buffer_17
  assign pull_resistor_18_node = _18 ? 32'h20000 : 32'bz;  // Controlled_Buffer controlled_buffer_18
  assign pull_resistor_19_node = _19 ? 32'h40000 : 32'bz;  // Controlled_Buffer controlled_buffer_19
  assign pull_resistor_20_node = _20 ? 32'h80000 : 32'bz;  // Controlled_Buffer controlled_buffer_20
  assign pull_resistor_21_node = _21 ? 32'h100000 : 32'bz;  // Controlled_Buffer controlled_buffer_21
  assign pull_resistor_22_node = _22 ? 32'h200000 : 32'bz;  // Controlled_Buffer controlled_buffer_22
  assign pull_resistor_23_node = _23 ? 32'h400000 : 32'bz;  // Controlled_Buffer controlled_buffer_23
  assign pull_resistor_24_node = _24 ? 32'h800000 : 32'bz;  // Controlled_Buffer controlled_buffer_24
  assign pull_resistor_25_node = _25 ? 32'h1000000 : 32'bz;  // Controlled_Buffer controlled_buffer_25
  assign pull_resistor_26_node = _26 ? 32'h2000000 : 32'bz;  // Controlled_Buffer controlled_buffer_26
  assign pull_resistor_27_node = _27 ? 32'h4000000 : 32'bz;  // Controlled_Buffer controlled_buffer_27
  assign pull_resistor_28_node = _28 ? 32'h8000000 : 32'bz;  // Controlled_Buffer controlled_buffer_28
  assign pull_resistor_29_node = _29 ? 32'h10000000 : 32'bz;  // Controlled_Buffer controlled_buffer_29
  assign pull_resistor_30_node = _30 ? 32'h20000000 : 32'bz;  // Controlled_Buffer controlled_buffer_30
  assign pull_resistor_31_node = _31 ? 32'h40000000 : 32'bz;  // Controlled_Buffer controlled_buffer_31
  assign pull_resistor_32_node = _32 ? 32'h80000000 : 32'bz;  // Controlled_Buffer controlled_buffer_32
  assign n1 = pull_resistor_1_node & colods;  // AND_Gate and_2, 32 bits wide
  assign n2 = pull_resistor_2_node & colods;  // AND_Gate and_3, 32 bits wide
  assign n3 = pull_resistor_3_node & colods;  // AND_Gate and_4, 32 bits wide
  assign n4 = pull_resistor_4_node & colods;  // AND_Gate and_5, 32 bits wide
  assign n5 = pull_resistor_5_node & colods;  // AND_Gate and_6, 32 bits wide
  assign n6 = pull_resistor_6_node & colods;  // AND_Gate and_7, 32 bits wide
  assign n7 = pull_resistor_7_node & colods;  // AND_Gate and_8, 32 bits wide
  assign n8 = pull_resistor_8_node & colods;  // AND_Gate and_9, 32 bits wide
  assign n9 = pull_resistor_9_node & colods;  // AND_Gate and_10, 32 bits wide
  assign n10 = pull_resistor_10_node & colods;  // AND_Gate and_11, 32 bits wide
  assign n11 = pull_resistor_11_node & colods;  // AND_Gate and_12, 32 bits wide
  assign n12 = pull_resistor_12_node & colods;  // AND_Gate and_13, 32 bits wide
  assign n13 = pull_resistor_13_node & colods;  // AND_Gate and_14, 32 bits wide
  assign n14 = pull_resistor_14_node & colods;  // AND_Gate and_15, 32 bits wide
  assign n15 = pull_resistor_15_node & colods;  // AND_Gate and_16, 32 bits wide
  assign n16 = pull_resistor_16_node & colods;  // AND_Gate and_17, 32 bits wide
  assign n17 = pull_resistor_17_node & colods;  // AND_Gate and_18, 32 bits wide
  assign n18 = pull_resistor_18_node & colods;  // AND_Gate and_19, 32 bits wide
  assign n19 = pull_resistor_19_node & colods;  // AND_Gate and_20, 32 bits wide
  assign n20 = pull_resistor_20_node & colods;  // AND_Gate and_21, 32 bits wide
  assign n21 = pull_resistor_21_node & colods;  // AND_Gate and_22, 32 bits wide
  assign n22 = pull_resistor_22_node & colods;  // AND_Gate and_23, 32 bits wide
  assign n23 = pull_resistor_23_node & colods;  // AND_Gate and_24, 32 bits wide
  assign n24 = pull_resistor_24_node & colods;  // AND_Gate and_25, 32 bits wide
  assign n25 = pull_resistor_25_node & colods;  // AND_Gate and_26, 32 bits wide
  assign n26 = pull_resistor_26_node & colods;  // AND_Gate and_27, 32 bits wide
  assign n27 = pull_resistor_27_node & colods;  // AND_Gate and_28, 32 bits wide
  assign n28 = pull_resistor_28_node & colods;  // AND_Gate and_29, 32 bits wide
  assign n29 = pull_resistor_29_node & colods;  // AND_Gate and_30, 32 bits wide
  assign n30 = pull_resistor_30_node & colods;  // AND_Gate and_31, 32 bits wide
  assign n31 = pull_resistor_31_node & colods;  // AND_Gate and_32, 32 bits wide
  assign n32 = pull_resistor_32_node & colods;  // AND_Gate and_33, 32 bits wide
  BitFinder #(.width(32)) bitfinder_1 (.in(n1), .found(bitfinder_1_found));  // open: index
  BitFinder #(.width(32)) bitfinder_2 (.in(n2), .found(bitfinder_2_found));  // open: index
  BitFinder #(.width(32)) bitfinder_3 (.in(n3), .found(bitfinder_3_found));  // open: index
  BitFinder #(.width(32)) bitfinder_4 (.in(n4), .found(bitfinder_4_found));  // open: index
  BitFinder #(.width(32)) bitfinder_5 (.in(n5), .found(bitfinder_5_found));  // open: index
  BitFinder #(.width(32)) bitfinder_6 (.in(n6), .found(bitfinder_6_found));  // open: index
  BitFinder #(.width(32)) bitfinder_7 (.in(n7), .found(bitfinder_7_found));  // open: index
  BitFinder #(.width(32)) bitfinder_8 (.in(n8), .found(bitfinder_8_found));  // open: index
  BitFinder #(.width(32)) bitfinder_9 (.in(n9), .found(bitfinder_9_found));  // open: index
  BitFinder #(.width(32)) bitfinder_10 (.in(n10), .found(bitfinder_10_found));  // open: index
  BitFinder #(.width(32)) bitfinder_11 (.in(n11), .found(bitfinder_11_found));  // open: index
  BitFinder #(.width(32)) bitfinder_12 (.in(n12), .found(bitfinder_12_found));  // open: index
  BitFinder #(.width(32)) bitfinder_13 (.in(n13), .found(bitfinder_13_found));  // open: index
  BitFinder #(.width(32)) bitfinder_14 (.in(n14), .found(bitfinder_14_found));  // open: index
  BitFinder #(.width(32)) bitfinder_15 (.in(n15), .found(bitfinder_15_found));  // open: index
  BitFinder #(.width(32)) bitfinder_16 (.in(n16), .found(bitfinder_16_found));  // open: index
  BitFinder #(.width(32)) bitfinder_17 (.in(n17), .found(bitfinder_17_found));  // open: index
  BitFinder #(.width(32)) bitfinder_18 (.in(n18), .found(bitfinder_18_found));  // open: index
  BitFinder #(.width(32)) bitfinder_19 (.in(n19), .found(bitfinder_19_found));  // open: index
  BitFinder #(.width(32)) bitfinder_20 (.in(n20), .found(bitfinder_20_found));  // open: index
  BitFinder #(.width(32)) bitfinder_21 (.in(n21), .found(bitfinder_21_found));  // open: index
  BitFinder #(.width(32)) bitfinder_22 (.in(n22), .found(bitfinder_22_found));  // open: index
  BitFinder #(.width(32)) bitfinder_23 (.in(n23), .found(bitfinder_23_found));  // open: index
  BitFinder #(.width(32)) bitfinder_24 (.in(n24), .found(bitfinder_24_found));  // open: index
  BitFinder #(.width(32)) bitfinder_25 (.in(n25), .found(bitfinder_25_found));  // open: index
  BitFinder #(.width(32)) bitfinder_26 (.in(n26), .found(bitfinder_26_found));  // open: index
  BitFinder #(.width(32)) bitfinder_27 (.in(n27), .found(bitfinder_27_found));  // open: index
  BitFinder #(.width(32)) bitfinder_28 (.in(n28), .found(bitfinder_28_found));  // open: index
  BitFinder #(.width(32)) bitfinder_29 (.in(n29), .found(bitfinder_29_found));  // open: index
  BitFinder #(.width(32)) bitfinder_30 (.in(n30), .found(bitfinder_30_found));  // open: index
  BitFinder #(.width(32)) bitfinder_31 (.in(n31), .found(bitfinder_31_found));  // open: index
  BitFinder #(.width(32)) bitfinder_32 (.in(n32), .found(bitfinder_32_found));  // open: index
  Pull_Resistor pull_resistor_33 (.node(pull_resistor_33_node));
  assign pull_resistor_33_node = bitfinder_1_found ? 4'b0010 : 4'bz;  // Controlled_Buffer controlled_buffer_33
  Pull_Resistor pull_resistor_34 (.node(pull_resistor_34_node));
  assign pull_resistor_34_node = bitfinder_2_found ? 4'b0011 : 4'bz;  // Controlled_Buffer controlled_buffer_34
  Pull_Resistor pull_resistor_35 (.node(pull_resistor_35_node));
  assign pull_resistor_35_node = bitfinder_3_found ? 4'b0100 : 4'bz;  // Controlled_Buffer controlled_buffer_35
  Pull_Resistor pull_resistor_36 (.node(pull_resistor_36_node));
  assign pull_resistor_36_node = bitfinder_4_found ? 4'b0101 : 4'bz;  // Controlled_Buffer controlled_buffer_36
  Pull_Resistor pull_resistor_37 (.node(pull_resistor_37_node));
  assign pull_resistor_37_node = bitfinder_5_found ? 4'b0110 : 4'bz;  // Controlled_Buffer controlled_buffer_37
  Pull_Resistor pull_resistor_38 (.node(pull_resistor_38_node));
  assign pull_resistor_38_node = bitfinder_6_found ? 4'b0111 : 4'bz;  // Controlled_Buffer controlled_buffer_38
  Pull_Resistor pull_resistor_39 (.node(pull_resistor_39_node));
  assign pull_resistor_39_node = bitfinder_7_found ? 4'b1000 : 4'bz;  // Controlled_Buffer controlled_buffer_39
  Pull_Resistor pull_resistor_40 (.node(pull_resistor_40_node));
  assign pull_resistor_40_node = bitfinder_8_found ? 4'b1001 : 4'bz;  // Controlled_Buffer controlled_buffer_40
  Pull_Resistor pull_resistor_41 (.node(pull_resistor_41_node));
  assign pull_resistor_41_node = bitfinder_9_found ? 4'b0010 : 4'bz;  // Controlled_Buffer controlled_buffer_41
  Pull_Resistor pull_resistor_42 (.node(pull_resistor_42_node));
  assign pull_resistor_42_node = bitfinder_10_found ? 4'b0011 : 4'bz;  // Controlled_Buffer controlled_buffer_42
  Pull_Resistor pull_resistor_43 (.node(pull_resistor_43_node));
  assign pull_resistor_43_node = bitfinder_11_found ? 4'b0100 : 4'bz;  // Controlled_Buffer controlled_buffer_43
  Pull_Resistor pull_resistor_44 (.node(pull_resistor_44_node));
  assign pull_resistor_44_node = bitfinder_12_found ? 4'b0101 : 4'bz;  // Controlled_Buffer controlled_buffer_44
  Pull_Resistor pull_resistor_45 (.node(pull_resistor_45_node));
  assign pull_resistor_45_node = bitfinder_13_found ? 4'b0110 : 4'bz;  // Controlled_Buffer controlled_buffer_45
  Pull_Resistor pull_resistor_46 (.node(pull_resistor_46_node));
  assign pull_resistor_46_node = bitfinder_14_found ? 4'b0111 : 4'bz;  // Controlled_Buffer controlled_buffer_46
  Pull_Resistor pull_resistor_47 (.node(pull_resistor_47_node));
  assign pull_resistor_47_node = bitfinder_15_found ? 4'b1000 : 4'bz;  // Controlled_Buffer controlled_buffer_47
  Pull_Resistor pull_resistor_48 (.node(pull_resistor_48_node));
  assign pull_resistor_48_node = bitfinder_16_found ? 4'b1001 : 4'bz;  // Controlled_Buffer controlled_buffer_48
  Pull_Resistor pull_resistor_49 (.node(pull_resistor_49_node));
  assign pull_resistor_49_node = bitfinder_17_found ? 4'b0010 : 4'bz;  // Controlled_Buffer controlled_buffer_49
  Pull_Resistor pull_resistor_50 (.node(pull_resistor_50_node));
  assign pull_resistor_50_node = bitfinder_18_found ? 4'b0011 : 4'bz;  // Controlled_Buffer controlled_buffer_50
  Pull_Resistor pull_resistor_51 (.node(pull_resistor_51_node));
  assign pull_resistor_51_node = bitfinder_19_found ? 4'b0100 : 4'bz;  // Controlled_Buffer controlled_buffer_51
  Pull_Resistor pull_resistor_52 (.node(pull_resistor_52_node));
  assign pull_resistor_52_node = bitfinder_20_found ? 4'b0101 : 4'bz;  // Controlled_Buffer controlled_buffer_52
  Pull_Resistor pull_resistor_53 (.node(pull_resistor_53_node));
  assign pull_resistor_53_node = bitfinder_21_found ? 4'b0110 : 4'bz;  // Controlled_Buffer controlled_buffer_53
  Pull_Resistor pull_resistor_54 (.node(pull_resistor_54_node));
  assign pull_resistor_54_node = bitfinder_22_found ? 4'b0111 : 4'bz;  // Controlled_Buffer controlled_buffer_54
  Pull_Resistor pull_resistor_55 (.node(pull_resistor_55_node));
  assign pull_resistor_55_node = bitfinder_23_found ? 4'b1000 : 4'bz;  // Controlled_Buffer controlled_buffer_55
  Pull_Resistor pull_resistor_56 (.node(pull_resistor_56_node));
  assign pull_resistor_56_node = bitfinder_24_found ? 4'b1001 : 4'bz;  // Controlled_Buffer controlled_buffer_56
  Pull_Resistor pull_resistor_57 (.node(pull_resistor_57_node));
  assign pull_resistor_57_node = bitfinder_25_found ? 4'b0010 : 4'bz;  // Controlled_Buffer controlled_buffer_57
  Pull_Resistor pull_resistor_58 (.node(pull_resistor_58_node));
  assign pull_resistor_58_node = bitfinder_26_found ? 4'b0011 : 4'bz;  // Controlled_Buffer controlled_buffer_58
  Pull_Resistor pull_resistor_59 (.node(pull_resistor_59_node));
  assign pull_resistor_59_node = bitfinder_27_found ? 4'b0100 : 4'bz;  // Controlled_Buffer controlled_buffer_59
  Pull_Resistor pull_resistor_60 (.node(pull_resistor_60_node));
  assign pull_resistor_60_node = bitfinder_28_found ? 4'b0101 : 4'bz;  // Controlled_Buffer controlled_buffer_60
  Pull_Resistor pull_resistor_61 (.node(pull_resistor_61_node));
  assign pull_resistor_61_node = bitfinder_29_found ? 4'b0110 : 4'bz;  // Controlled_Buffer controlled_buffer_61
  Pull_Resistor pull_resistor_62 (.node(pull_resistor_62_node));
  assign pull_resistor_62_node = bitfinder_30_found ? 4'b0111 : 4'bz;  // Controlled_Buffer controlled_buffer_62
  Pull_Resistor pull_resistor_63 (.node(pull_resistor_63_node));
  assign pull_resistor_63_node = bitfinder_31_found ? 4'b1000 : 4'bz;  // Controlled_Buffer controlled_buffer_63
  Pull_Resistor pull_resistor_64 (.node(pull_resistor_64_node));
  assign pull_resistor_64_node = bitfinder_32_found ? 4'b1001 : 4'bz;  // Controlled_Buffer controlled_buffer_64
  assign card = pull_resistor_33_node | pull_resistor_34_node | pull_resistor_35_node | pull_resistor_36_node | pull_resistor_37_node | pull_resistor_38_node | pull_resistor_39_node | pull_resistor_40_node | pull_resistor_41_node | pull_resistor_42_node | pull_resistor_43_node | pull_resistor_44_node | pull_resistor_45_node | pull_resistor_46_node | pull_resistor_47_node | pull_resistor_48_node | pull_resistor_49_node | pull_resistor_50_node | pull_resistor_51_node | pull_resistor_52_node | pull_resistor_53_node | pull_resistor_54_node | pull_resistor_55_node | pull_resistor_56_node | pull_resistor_57_node | pull_resistor_58_node | pull_resistor_59_node | pull_resistor_60_node | pull_resistor_61_node | pull_resistor_62_node | pull_resistor_63_node | pull_resistor_64_node;  // OR_Gate or_1, 4 bits wide
endmodule

module generator (
  input  clock,
  input  reset,
  output [7:0] address,
  output [7:0] data,
  output l_d,
  output clock_gen,
  output gen_done
);

  wire bitfinder_1_found, comparator_1_eq, comparator_2_eq, comparator_3_eq, comparator_4_eq,
       comparator_5_eq, comparator_6_eq, comparator_7_eq, comparator_8_gt, comparator_9_eq, comparator_10_eq,
       comparator_12_eq, eq_0, not_1_out, not_2_out, not_3_out, not_4_out, not_5_out, or_1_out, or_2_out,
       tact;
  wire [3:0] configuration_1_card;
  wire [4:0] adder_1_out, multiplexer_2_out, register_1_q;
  wire [7:0] addr, counter_1_q, counter_2_q;
  wire [7:7] pull_resistor_1_node;
  wire [31:0] configuration_1_final_colod, multiplexer_3_out, multiplexer_4_out, pull_resistor_2_node;

  Multiplexer #(.select(5), .width(8), .disabled(0), .enable("false")) multiplexer_1 (
    .in0(8'h91), .in1(8'h92), .in2(8'h9a), .in3(8'h9b), .in4(8'h9c), .in5(8'ha4), .in6(8'ha5), .in7(8'ha6),
    .in8(8'ha7), .in9(8'haf), .in10(8'hb0), .in11(8'hb1), .in12(8'hb2), .in13(8'hb3), .in14(8'hbb),
    .in15(8'hbc), .in16(8'hbd), .in17(8'hbe), .in18(8'hbf), .in19(8'hc8), .in20(8'hc9), .in21(8'hca),
    .in22(8'hcb), .in23(8'hcc), .in24(8'hcd), .in25(8'hd6), .in26(8'hd7), .in27(8'hd8), .in28(8'hd9),
    .in29(8'hda), .in30(8'hdb), .in31(8'hdc), .out(addr), .sel(register_1_q));
  Multiplexer #(.width(5), .enable("false")) multiplexer_2 (
    .in0({5{1'b0}}), .in1(adder_1_out), .out(multiplexer_2_out), .sel(comparator_8_gt));
  and and_1 (tact, clock, gen_done);
  Adder #(.width(5)) adder_1 (.a(register_1_q), .b(5'b00001), .out(adder_1_out));  // open: cin, cout
  not not_1 (not_1_out, eq_0);
  Counter counter_1 (.D({8{1'b0}}), .Q(counter_1_q), .clk(tact), .clr(reset));  // open: load, count, carry
  Comparator comparator_1 (.a(8'h92), .b(addr), .eq(comparator_1_eq));  // open: gt, lt
  Comparator comparator_2 (.a(8'h9c), .b(addr), .eq(comparator_2_eq));  // open: gt, lt
  Comparator comparator_3 (.a(8'ha7), .b(addr), .eq(comparator_3_eq));  // open: gt, lt
  Comparator comparator_4 (.a(8'hb3), .b(addr), .eq(comparator_4_eq));  // open: gt, lt
  Comparator comparator_5 (.a(8'hbf), .b(addr), .eq(comparator_5_eq));  // open: gt, lt
  Comparator comparator_6 (.a(8'hcd), .b(addr), .eq(comparator_6_eq));  // open: gt, lt
  Comparator comparator_7 (.a(8'hdc), .b(addr), .eq(comparator_7_eq));  // open: gt, lt
  Register #(.width(5)) register_1 (
    .D(multiplexer_2_out), .en(not_1_out), .Q(register_1_q), .clk(not_2_out), .clr(reset));
  not not_2 (not_2_out, tact);
  Comparator #(.mode("unsigned")) comparator_8 (.a(counter_1_q), .b({8{1'b0}}), .gt(comparator_8_gt));  // open: eq, lt
  or or_1 (or_1_out, gen_done, comparator_9_eq);
  or or_2 (or_2_out, comparator_1_eq, comparator_2_eq, comparator_3_eq, comparator_4_eq, comparator_5_eq, comparator_6_eq, comparator_7_eq);
  Multiplexer #(.width(32)) multiplexer_3 (
    .in0({32{1'b1}}), .in1(multiplexer_4_out), .out(multiplexer_3_out), .sel(not_3_out));  // open: en
  Counter counter_2 (.Q(counter_2_q), .clk(tact), .clr(reset));  // open: load, D, count, carry
  assign address = or_1_out ? addr : 8'bz;  // Controlled_Buffer controlled_buffer_1
  Comparator #(.mode("unsigned")) comparator_9 (.a(8'hdc), .b(addr), .eq(comparator_9_eq));  // open: gt, lt
  Pull_Resistor #(.pull(1)) pull_resistor_1 (.node(pull_resistor_1_node[7]));
  assign pull_resistor_1_node[7] = or_2_out ? 1'b0 : 1'bz;  // Controlled_Buffer controlled_buffer_2
  Pull_Resistor #(.pull(1)) pull_resistor_2 (.node(pull_resistor_2_node));
  assign pull_resistor_2_node = bitfinder_1_found ? multiplexer_3_out : 32'bz;  // Controlled_Buffer controlled_buffer_3
  not not_3 (not_3_out, comparator_10_eq);
  Comparator #(.mode("unsigned")) comparator_10 (
    .a({8{1'b0}}), .b(counter_2_q), .eq(comparator_10_eq));  // open: gt, lt
  BitFinder bitfinder_1 (.in(counter_2_q), .found(bitfinder_1_found));  // open: index
  configuration configuration_1 (
    .colods(pull_resistor_2_node), .clock(clock), .final_colod(configuration_1_final_colod),
    .card(configuration_1_card));
  Multiplexer #(.width(32), .enable("false")) multiplexer_4 (
    .in0(pull_resistor_2_node), .in1(configuration_1_final_colod), .out(multiplexer_4_out), .sel(not_4_out));
  not not_4 (not_4_out, clock);
  assign l_d = gen_done ? eq_0 : 1'bz;  // Controlled_Buffer controlled_buffer_4
  assign clock_gen = gen_done ? not_5_out : 1'bz;  // Controlled_Buffer controlled_buffer_5
  not not_5 (not_5_out, clock);
  Hex_Digit_Display hex_digit_display_1 (.value(configuration_1_card));  // open: dp
  assign data = gen_done ? {pull_resistor_1_node[7], 3'b100, configuration_1_card} : 8'bz;  // Controlled_Buffer controlled_buffer_6
  Comparator #(.width(4)) comparator_11 (.a(4'b0000), .b(configuration_1_card), .eq(eq_0));  // open: gt, lt
  Comparator #(.width(32)) comparator_12 (
    .a({32{1'b0}}), .b(multiplexer_4_out), .eq(comparator_12_eq));  // open: gt, lt
  not not_6 (gen_done, comparator_12_eq);

  // Notes on the sheet:
  //   1 colon
  //   2 colon
  //   3 colon
  //   4 colon
  //   5 colon
  //   6 colon
  //   7 colon
  //   opened
  //   sentinels
  //   Купил нисан - ебись с ним сам
endmodule

module write_sentinels (
  input  clock,
  input  reset,
  output [7:0] address,
  output [7:0] data,
  output l_d,
  output clock_gen
);

  wire comparator_1_gt, comparator_2_eq, gen_done, not_1_out, not_2_out, tact;
  wire [2:0] adder_1_out, multiplexer_2_out, register_1_q;
  wire [7:0] addr, counter_1_q;

  Multiplexer #(.select(3), .width(8), .disabled(0), .enable("false")) multiplexer_1 (
    .in0(8'h90), .in1(8'h99), .in2(8'ha3), .in3(8'hae), .in4(8'hba), .in5(8'hc7), .in6(8'hd5),
    .in7({8{1'b1}}), .out(addr), .sel(register_1_q));
  Multiplexer #(.width(3), .enable("false")) multiplexer_2 (
    .in0(3'b000), .in1(adder_1_out), .out(multiplexer_2_out), .sel(comparator_1_gt));
  Counter counter_1 (.D({8{1'b0}}), .Q(counter_1_q), .clk(tact), .clr(reset));  // open: load, count, carry
  Adder #(.width(3)) adder_1 (.a(register_1_q), .b(3'b001), .out(adder_1_out));  // open: cin, cout
  Register #(.width(3)) register_1 (
    .D(multiplexer_2_out), .en(gen_done), .Q(register_1_q), .clk(not_1_out), .clr(reset));
  not not_1 (not_1_out, tact);
  assign address = gen_done ? addr : 8'bz;  // Controlled_Buffer controlled_buffer_1
  assign l_d = gen_done ? 1'b0 : 1'bz;  // Controlled_Buffer controlled_buffer_2
  assign clock_gen = gen_done ? not_2_out : 1'bz;  // Controlled_Buffer controlled_buffer_3
  not not_2 (not_2_out, clock);
  Comparator #(.mode("unsigned")) comparator_1 (.a(counter_1_q), .b({8{1'b0}}), .gt(comparator_1_gt));  // open: eq, lt
  assign data = gen_done ? 8'ha : 8'bz;  // Controlled_Buffer controlled_buffer_4
  Comparator #(.mode("unsigned")) comparator_2 (.a({8{1'b1}}), .b(addr), .eq(comparator_2_eq));  // open: gt, lt
  and and_1 (tact, clock, gen_done);
  not not_3 (gen_done, comparator_2_eq);

  // Notes on the sheet:
  //   Купил нисан - ебись с ним сам
  //   opened
  //   sentinels
endmodule
